# Fritzing sketch growmat_easy_05dm2 (saved by Fritzing 0.9.2b)
circuit board: 9cm x 5.5cm
breadboards: 1

parts:
  LCM1602_IIC1 = LCM1602 IIC [part_number="LCM1602 IIC" chip_label="LCM1602 IIC" package="DIP (Dual Inline) [THT]"]
  LCD1 = LCD screen SD1602VBWB-XA-G-G
  Keypad4x1 = Keypad Membran 4x4
  Part1 = Arduino Nano (Rev3.0)
  GSM_SIM_GPSR_SMS_SIM900_SIM1 = SIM800L [package=THT]
  J1 = screw terminal, 4 pins
  Tiny_RTC3 = Tiny RTC
  J2 = screw terminal, 4 pins
  J3 = screw terminal, 3 pins
  J4 = female pin header, 6 pins [form="♀ (female)"]
  J5 = female pin header, 4 pins [form="♀ (female)"]
  C2 = Capacitor [package=cap-pth-small2]
  C4 = Capacitor Polarized [package=cpol-radial-10uf-25v]
  X1 = USB Connectors [package=usb-a-h]
  Pad1 = Pad [width=3.29987138112835 height=14.5664585819167 connect=center]  # not connected
  R2 = Resistor [tolerance=±5% resistance=220 package=THT]
  R3 = Resistor [tolerance=±5% resistance=220 package=THT]

nets:
  N1: LCM1602_IIC1.VSS, LCD1.LED+
  N2: LCM1602_IIC1.VDD, LCD1.LED-
  N3: LCM1602_IIC1.V0, LCD1.VSS
  N4: LCM1602_IIC1.RS, LCD1.VDD
  N5: LCM1602_IIC1.RW, LCD1.V0
  N6: LCM1602_IIC1.E, LCD1.RS
  N7: LCM1602_IIC1.D0, LCD1.R/W
  N8: LCM1602_IIC1.D1, LCD1.E
  N9: LCM1602_IIC1.D2, LCD1.DB0
  N10: LCM1602_IIC1.D3, LCD1.DB1
  N11: LCM1602_IIC1.D4, LCD1.DB2
  N12: LCM1602_IIC1.D5, LCD1.DB3
  N13: LCM1602_IIC1.D6, LCD1.DB4
  N14: LCM1602_IIC1.D7, LCD1.DB5
  N15: LCM1602_IIC1.A, LCD1.DB6
  N16: Keypad4x1.Pin1, Keypad4x1.Pin2, Keypad4x1.Pin3, Keypad4x1.Pin4, Keypad4x1.Pin7, Keypad4x1.Pin8
  GND: Part1.GND, GSM_SIM_GPSR_SMS_SIM900_SIM1.GND, J1.pin2, Tiny_RTC3.GND#10, J2.pin2, J3.pin2, J4.pin6, J5.pin2, C2.2, C4.-, X1.GND, R2.Pin_1
  N17: Part1.D2, GSM_SIM_GPSR_SMS_SIM900_SIM1.SIM_TXD
  N18: Part1.D3, GSM_SIM_GPSR_SMS_SIM900_SIM1.SIM_RXD
  N19: Part1.D4, GSM_SIM_GPSR_SMS_SIM900_SIM1.RST
  N20: Part1.D5, J2.pin4
  N21: Part1.D6, J1.pin4
  N22: Part1.D7, R2.Pin_0, R3.Pin_1
  N23: Part1.D9, J4.pin5
  N24: Part1.D10, J4.pin4
  N25: Part1.D11/MOSI, J4.pin3
  N26: Part1.D12/MISO, J4.pin2
  VIN: Part1.VIN, GSM_SIM_GPSR_SMS_SIM900_SIM1.5V, J1.pin1, J2.pin1, J3.pin1, J4.pin1, C2.1, C4.+, X1.VBUS
  N27: Part1.5V, Tiny_RTC3.VCC#9, J5.pin1
  N28: Part1.A5, Tiny_RTC3.SCL#7, J5.pin4
  N29: Part1.A4, Tiny_RTC3.SDA#8, J5.pin3
  N30: Part1.A1, J2.pin3
  N31: Part1.A0, J1.pin3
  N32: J3.pin3, R3.Pin_0

notes:
  5V
  GND
  A1
  D5
  A0
  D6
  D7
  5
  G
  D2
  D3
  D4
  SIM800L
  RTC
  GROWMAT
  3.7
  SENSOR
  EXT
  EASY rev1
  bcsedlon@  gmail.com

custom parts:
  LCM1602 IIC: I2C-Module to use a 1602 or 2004 LCD on with the wire.h libory Serial LCD Modul
  LCD screen SD1602VBWB-XA-G-G: A standard character display, usually with 2x16 characters based on Lionel Michel's LCD display.
  Keypad Membran 4x4: Membrane Keypad 4x4 Matrix
  Tiny RTC: Tiny RTC I2C module DS1370Z RTC and AT24C32 EEPROM
