# Fritzing sketch growmat_easy_rev2a (saved by Fritzing 0.9.2b)
circuit board: 10cm x 5cm
breadboards: 1

parts:
  RTC = RTC DS1307 bcsedlon
  SIM800L = SIM800L bcsedlon [package=THT]
  TP4056 = TP4056 bcsedlon [package=THT]
  DC-DC = DC-DC bcsedlon [package=THT]
  NANO = Arduino Nano (Rev3.0)
  OUT = male pin header, 6 pins [form="♂ (male)"]
  J2 = Power Jack [package=power_jack_slot]
  I2C = male pin header, 4 pins [form="♂ (male)"]
  I2C1 = male pin header, 5 pins [form="♂ (male)"]
  BAT2 = male pin header, 3 pins [form="♂ (male)"]
  BAT5 = male pin header, 3 pins [form="♂ (male)"]
  BAT6 = male pin header, 2 pins [form="♂ (male)"]  # not connected
  BAT = male pin header, 4 pins [form="♂ (male)"]
  BAT7 = male pin header, 2 pins [form="♂ (male)"]
  J1 = screw terminal, 5 pins
  R1 = Resistor [tolerance=±5% resistance=100k package=THT]
  R2 = Resistor [tolerance=±5% resistance=220 package=THT]
  R4 = Resistor [tolerance=±5% resistance=220 package=THT]

nets:
  N1: RTC.SCL#1, I2C.pin4
  N2: RTC.SDA#2, I2C.pin3
  N3: RTC.VCC#3, I2C.pin1, BAT5.pin3
  N4: RTC.GND#4, I2C.pin2
  N5: RTC.SCL#7, NANO.A5
  N6: RTC.SDA#8, NANO.A4
  5V: RTC.VCC#9, SIM800L.5V, DC-DC.VOUT+, NANO.5V, J1.pin5
  N7: RTC.GND#10, SIM800L.GND#5, TP4056.VOUT-, DC-DC.VOUT-, DC-DC.VIN-, NANO.GND, OUT.pin1, J1.pin4
  N8: SIM800L.GND#1, BAT7.pin1
  N9: SIM800L.VDD, BAT7.pin2
  N10: SIM800L.SIM_TXD, NANO.D8
  N11: SIM800L.SIM_RXD, NANO.D7
  N12: SIM800L.RST, NANO.D5
  N13: TP4056.VOUT+, DC-DC.VIN+
  N14: TP4056.VBAT+, BAT.pin1, BAT.pin2, R1.Pin_0
  N15: TP4056.VBAT-, BAT.pin3, BAT.pin4
  N16: TP4056.VIN-, J2.GND
  N17: TP4056.VIN+, NANO.A2, J2.PWR, BAT5.pin1
  N18: NANO.D1/TX, BAT2.pin1
  N19: NANO.D0/RX, BAT2.pin2
  N20: NANO.RESET, BAT2.pin3
  N21: NANO.D2, R4.Pin_0
  N22: NANO.D3, R2.Pin_0
  N23: NANO.D9, OUT.pin2
  N24: NANO.D10, OUT.pin3
  N25: NANO.D11/MOSI, OUT.pin4
  N26: NANO.D12/MISO, OUT.pin5
  N27: NANO.A7, J1.pin3
  N28: NANO.A3, R1.Pin_1
  N29: NANO.A1, I2C1.pin1
  N30: NANO.A0, I2C1.pin2
  N31: NANO.AREF, I2C1.pin3
  N32: NANO.3V3, I2C1.pin4
  N33: NANO.D13/SCK, I2C1.pin5
  N34: OUT.pin6, BAT5.pin2
  N35: J1.pin1, R4.Pin_1
  N36: J1.pin2, R2.Pin_1

notes:
  +
  -
  D2
  A7
  GROWMAT EASY
  rev2a
  SDA
  SCL
  D3
  BAT

custom parts:
  RTC DS1307 bcsedlon: Tiny RTC I2C module DS1370Z RTC and AT24C32 EEPROM
  SIM800L bcsedlon: Approximation of SIM800L, a simple GSM module.
  TP4056 bcsedlon: Approximation of TP4056 module.
  DC-DC bcsedlon: Approximation of TP4056 module.
