# Fritzing sketch growmat_easy_rev2b (saved by Fritzing 0.9.2b)
circuit board: 10cm x 5cm
breadboards: 1

parts:
  RTC = RTC DS1307 bcsedlon
  SIM800L = SIM800L bcsedlon [package=THT]
  TP4056 = TP4056 bcsedlon [package=THT]
  DC-DC = DC-DC bcsedlon [package=THT]
  NANO = Arduino Nano (Rev3.0)
  OUT = male pin header, 6 pins [form="♂ (male)"]
  J2 = Power Jack [package=power_jack_slot]
  I2C = male pin header, 4 pins [form="♂ (male)"]
  I2C1 = male pin header, 5 pins [form="♂ (male)"]
  BAT2 = male pin header, 3 pins [form="♂ (male)"]
  BAT5 = male pin header, 3 pins [form="♂ (male)"]
  BAT = male pin header, 4 pins [form="♂ (male)"]
  J1 = screw terminal, 5 pins
  R1 = Resistor [tolerance=±5% resistance=100k package=THT]
  R2 = Resistor [tolerance=±5% resistance=220 package=THT]
  R3 = Resistor [tolerance=±5% resistance=220 package=THT]

nets:
  N1: RTC.SCL#1, I2C.pin4
  N2: RTC.SDA#2, I2C.pin3
  N3: RTC.VCC#3, I2C.pin1, BAT5.pin3
  N4: RTC.GND#4, I2C.pin2
  N5: RTC.SCL#7, NANO.A5
  N6: RTC.SDA#8, NANO.A4
  5V: RTC.VCC#9, SIM800L.5V, DC-DC.VOUT+, NANO.5V, J1.pin5
  GND: RTC.GND#10, SIM800L.GND, TP4056.VOUT-, DC-DC.VOUT-, DC-DC.VIN-, NANO.GND, OUT.pin6, J1.pin4
  N7: SIM800L.SIM_TXD, NANO.D2
  N8: SIM800L.SIM_RXD, NANO.D3
  N9: SIM800L.RST, NANO.D4
  N10: TP4056.VOUT+, DC-DC.VIN+
  N11: TP4056.VBAT+, BAT.pin1, BAT.pin2, R1.Pin_0
  N12: TP4056.VBAT-, BAT.pin3, BAT.pin4
  N13: TP4056.VIN-, J2.GND
  N14: TP4056.VIN+, NANO.A2, J2.PWR, BAT5.pin1
  N15: NANO.D1/TX, BAT2.pin1
  N16: NANO.D0/RX, BAT2.pin2
  N17: NANO.RESET, BAT2.pin3
  N18: NANO.D7, R3.Pin_0
  N19: NANO.D8, R2.Pin_0
  N20: NANO.D9, OUT.pin2
  N21: NANO.D10, OUT.pin3
  N22: NANO.D11/MOSI, OUT.pin4
  N23: NANO.D12/MISO, OUT.pin5
  N24: NANO.A7, J1.pin3
  N25: NANO.A3, R1.Pin_1
  N26: NANO.A1, I2C1.pin1
  N27: NANO.A0, I2C1.pin2
  N28: NANO.AREF, I2C1.pin3
  N29: NANO.3V3, I2C1.pin4
  N30: NANO.D13/SCK, I2C1.pin5
  N31: OUT.pin1, BAT5.pin2
  N32: J1.pin1, R3.Pin_1
  N33: J1.pin2, R2.Pin_1

notes:
  +
  -
  D7
  A7
  GROWMAT EASY
  rev2b
  SDA
  SCL
  D8
  BAT

custom parts:
  RTC DS1307 bcsedlon: Tiny RTC I2C module DS1370Z RTC and AT24C32 EEPROM
  SIM800L bcsedlon: Approximation of SIM800L, a simple GSM module.
  TP4056 bcsedlon: Approximation of TP4056 module.
  DC-DC bcsedlon: Approximation of TP4056 module.
